# Fritzing sketch Breadboard (saved by Fritzing 0.9.3b)
breadboards: 1

parts:
  R1 = Resistor [tolerance=±5% resistance=22k package=THT]
  R2 = Resistor [tolerance=±5% resistance=10k package=THT]
  R3 = Resistor [tolerance=±5% resistance=10k package=THT]
  U1 = NodeMCU V1.0
  Grove1 = Catalex 4 Digit Display
  J1 = Piezo Speaker
  S1 = Pushbutton [package="[THT]"]
  R4 = Resistor [tolerance=±5% resistance=10k package=THT]
  U5 = TP4056 - Li-Ion Charger Module [chip_label=TP4056 package=THT]
  BAT = 18650 Size Battery in Holder [package=battery-18650]
  U4 = Voltage Regulator - 3.3V [package="TO220 [THT]"]

nets:
  N1: R1.Pin_0, R3.Pin_1
  N2: R1.Pin_1, U5.BAT+, BAT.+, U4.output_voltage
  N3: R2.Pin_1, R3.Pin_0, U1.A0
  N4: U1.D0, J1.pin2
  N5: U1.D1, S1.Pin_3, S1.Pin_4, R4.Pin_0
  N6: U1.3V3, S1.Pin_1, S1.Pin_2, U4.input_voltage
  GND: U1.GND, Grove1.GND, J1.pin1, R4.Pin_1, U5.IN-, BAT.-, U4.GND
  N7: U1.D5, Grove1.VCC
  N8: U1.D6, Grove1.DIO
  N9: U1.D7, Grove1.CLK
  N10: U1.Vin, U5.IN+

custom parts:
  NodeMCU V1.0: ESP8266 based NodeMCU
  Catalex 4 Digit Display: A 4 7-seg display
  TP4056 - Li-Ion Charger Module: TP4056. With 4 pins on a 100 mil inline pin header footprint.
  18650 Size Battery in Holder: Battery Holder with an 18650 size battery.
